# Fritzing sketch schematic (saved by Fritzing 0.9.3b)
breadboards: 1

parts:
  Bauteil1 = Arduino Nano (Rev3.0) (ICSP)
  DFRobot_DFPlayer_Mini1 = DFRobot DFPlayer Mini [part_number=DFR0299]
  SP1 = SPEAKER [package=pcb_mount_speaker]
  125_kHz_RFID_module1 = RDM6300
  Bauteil2 = RDM6300-ANT
  AMP1 = GF1002 Stereo Amplifier
  SP2 = SPEAKER [package=pcb_mount_speaker]
  S1 = Round Pushbutton
  S2 = Round Pushbutton
  Part1 = KY-006 Passive Buzzer Module [package="Breakout board"]
  R1 = Resistor [tolerance=±5% resistance=220 package=THT]

nets:
  N1: Bauteil1.GND, Bauteil1.D6, DFRobot_DFPlayer_Mini1.GND-1, DFRobot_DFPlayer_Mini1.GND-2, 125_kHz_RFID_module1.TX, 125_kHz_RFID_module1.GND#66, 125_kHz_RFID_module1.GND#67, AMP1.POWER-, AMP1.INPUTG, S1.leg1, S2.leg1, Part1.-
  N2: Bauteil1.D4, S2.leg0
  N3: Bauteil1.D5, S1.leg0
  N4: Bauteil1.D9, Part1.S
  N5: Bauteil1.D10, DFRobot_DFPlayer_Mini1.TX
  N6: Bauteil1.D11/MOSI, R1.Pin_0
  5V: Bauteil1.5V, DFRobot_DFPlayer_Mini1.VCC, 125_kHz_RFID_module1.+5V#65, AMP1.POWER+
  N7: DFRobot_DFPlayer_Mini1.RX, R1.Pin_1
  N8: DFRobot_DFPlayer_Mini1.DAC_R, AMP1.INPUTR
  N9: DFRobot_DFPlayer_Mini1.DAC_L, AMP1.INPUTL
  N10: SP1.+, AMP1.ROUT+
  N11: SP1.-, AMP1.ROUT-
  N12: 125_kHz_RFID_module1.ANT1, Bauteil2.ANT1
  N13: 125_kHz_RFID_module1.ANT2, Bauteil2.ANT2
  N14: AMP1.LOUT+, SP2.-
  N15: AMP1.LOUT-, SP2.+

custom parts:
  RDM6300: 125 kHz RFID module (serial interface)
  RDM6300-ANT: Antenna
  GF1002 Stereo Amplifier: GF1002 6 Watt Stereo Amplifier
  KY-006 Passive Buzzer Module: Passive Piezoelectric Buzzer Module Keyes KY-006, it can produce a range of sound tones depending on the input frequency.
